// Logisim project GeneradorPixeles.circ as structural Verilog: 1 circuit, main circuit GeneradorPixeles
module GeneradorPixeles (
  input  Start,
  input  Reset,
  input  Clock,
  output [3:0] X,
  output Fin,
  output [3:0] Y
);

  wire and_1_out, and_2_out, CarryX, CarryY, not_1_out, not_2_out;

  not not_1 (not_1_out, Fin);
  not not_2 (not_2_out, Fin);
  and and_1 (and_1_out, not_1_out, Start);
  and and_2 (and_2_out, CarryX, not_2_out);
  contadorX contadorx_1 (.Reset(Reset), .Enable(and_1_out), .Clock(Clock), .Carry(CarryX), .X(X));
  contadorY contadory_1 (.Reset(Reset), .Enable(and_2_out), .Clock(Clock), .Carry(CarryY), .Y(Y));
  and and_3 (Fin, CarryX, CarryY);
endmodule
