// Logisim project Rasterizador_grupo19.circ as structural Verilog: 3 circuits, main circuit main
module main (
  input  [3:0] A,
  input  [3:0] B,
  input  Start,
  input  Reset,
  input  Clock,
  input  [3:0] C,
  output Fin,
  output [15:0] RAM_F,
  output RAM_LED
);

  wire and_1_out, and_2_out, d_ff_1_qn, d_ff_2_qn, delayer_1_delayed_entry, Fin_t, not_1_out, Start_D;
  wire [3:0] X, Y;
  wire [15:0] calculof_1_valorf, decoder_1_out0, demultiplexer_1_out1, demultiplexer_1_out2,
       demultiplexer_1_out3, demultiplexer_1_out4, demultiplexer_1_out5, demultiplexer_1_out6,
       demultiplexer_1_out7, demultiplexer_1_out8, demultiplexer_1_out9, demultiplexer_1_out10,
       demultiplexer_1_out11, demultiplexer_1_out12, demultiplexer_1_out13, demultiplexer_1_out14,
       demultiplexer_1_out15, OFFSET;

  not not_1 (not_1_out, Fin);
  and and_1 (and_1_out, not_1_out, Start);
  GeneradorPixeles generadorpixeles_1 (.Clock(Clock), .Start(Start_D), .Reset(Reset), .X(X), .Y(Y), .Fin(Fin_t));
  // Probe on X
  CalculoF calculof_1 (
    .Clock(Clock), .Enable(Start), .C(C), .A(A), .B(B), .X(X), .Reset(Reset), .ValorF(calculof_1_valorf));
  EvaluadorYRAM evaluadoryram_1 (
    .Clock(Clock), .Enable(and_1_out), .F(calculof_1_valorf), .X(X), .Y(Y), .Reset(Reset), .RAM_LED(RAM_LED),
    .RAM_F(RAM_F));
  D_Flip_Flop d_ff_1 (.D(Fin_t), .clk(Clock), .Q(Fin), .Qn(d_ff_1_qn), .reset(Reset));  // open: preset
  D_Flip_Flop d_ff_2 (.D(Start), .clk(Clock), .Q(Start_D), .Qn(d_ff_2_qn), .reset(Reset));  // open: preset
  // NoConnect on d_ff_1_qn
  // NoConnect on d_ff_2_qn
  LED led_1 (.in(Fin));
  delayer delayer_1 (.Entry(Clock), .Delayed_Entry(delayer_1_delayed_entry));
  DotMatrix #(.matrixcols(16), .matrixrows(16), .persist(1000)) dotmatrix_1 (
    .col0(demultiplexer_1_out1), .col1(demultiplexer_1_out2), .col2(demultiplexer_1_out3),
    .col3(demultiplexer_1_out4), .col4(demultiplexer_1_out5), .col5(demultiplexer_1_out6),
    .col6(demultiplexer_1_out7), .col7(demultiplexer_1_out8), .col8(demultiplexer_1_out9),
    .col9(demultiplexer_1_out10), .col10(demultiplexer_1_out11), .col11(demultiplexer_1_out12),
    .col12(demultiplexer_1_out13), .col13(demultiplexer_1_out14), .col14(demultiplexer_1_out15),
    .col15(OFFSET));
  Demultiplexer #(.enable("true"), .select(4), .width(16)) demultiplexer_1 (
    .out0(OFFSET), .out1(demultiplexer_1_out1), .out2(demultiplexer_1_out2), .out3(demultiplexer_1_out3),
    .out4(demultiplexer_1_out4), .out5(demultiplexer_1_out5), .out6(demultiplexer_1_out6),
    .out7(demultiplexer_1_out7), .out8(demultiplexer_1_out8), .out9(demultiplexer_1_out9),
    .out10(demultiplexer_1_out10), .out11(demultiplexer_1_out11), .out12(demultiplexer_1_out12),
    .out13(demultiplexer_1_out13), .out14(demultiplexer_1_out14), .out15(demultiplexer_1_out15),
    .in(decoder_1_out0), .sel(X), .en(delayer_1_delayed_entry));
  and and_2 (and_2_out, Start_D, RAM_LED);
  Decoder #(.select(4)) decoder_1 (
    .out0(decoder_1_out0[0]), .out1(decoder_1_out0[1]), .out2(decoder_1_out0[2]), .out3(decoder_1_out0[3]),
    .out4(decoder_1_out0[4]), .out5(decoder_1_out0[5]), .out6(decoder_1_out0[6]), .out7(decoder_1_out0[7]),
    .out8(decoder_1_out0[8]), .out9(decoder_1_out0[9]), .out10(decoder_1_out0[10]),
    .out11(decoder_1_out0[11]), .out12(decoder_1_out0[12]), .out13(decoder_1_out0[13]),
    .out14(decoder_1_out0[14]), .out15(decoder_1_out0[15]), .sel(Y), .en(and_2_out));

  // Other names for the same wires on the sheet: CortarRam = Fin; R_LED = RAM_LED

  // Notes on the sheet:
  //   El generador de pixeles requiere habilitarse
  //   1 pulso de reloj mas tarde que el resto
  //   La ram corta 1 pulso de reloj mas tarde que la señal de corte
  //   y aumentando el numero conforme sube
  //   entrada recibida con X como selector
  //   Habilitar la salida del DMUX con un retraso es 
  //   Genera un numero de 16 bits con un 1 en la posicion equivalente a Y
  //   debido a la codificon de la altitud de la matriz led empezando con 0 abajo 
  //   Este DMUX determina a que columna pertenece la
  //   necesario ya que, debido a que el sumador toma mas tiempo en calcular f 
  //   que el generador de pixeles en pasar un nuevo x e y, la matriz prende pixeles
  //   nuevos con resultados viejos.
endmodule

module testing (
  input  Start,
  input  Reset,
  input  [3:0] A,
  input  [3:0] B,
  input  [3:0] C
);

  wire clock_1_out, main_1_fin, main_1_ram_led;
  wire [15:0] main_1_ram_f;

  Clock clock_1 (.out(clock_1_out));
  // Probe on main_1_fin
  // Probe on main_1_ram_f
  main main_1 (
    .Clock(clock_1_out), .Start(Start), .A(A), .B(B), .C(C), .Reset(Reset), .RAM_F(main_1_ram_f),
    .RAM_LED(main_1_ram_led), .Fin(main_1_fin));
  // Probe on main_1_ram_led
endmodule

module delayer (
  input  Entry,
  output Delayed_Entry
);

  wire and_1_out, and_2_out, and_3_out, and_4_out, and_5_out, and_6_out, and_7_out, and_8_out, and_9_out,
       and_10_out, and_11_out, and_12_out, and_13_out, and_14_out, and_15_out, and_16_out, and_17_out,
       and_18_out, and_19_out, and_20_out, and_22_out, and_23_out, and_24_out, and_25_out, and_26_out,
       and_27_out, and_28_out, and_29_out, and_30_out, and_31_out, and_32_out, and_33_out, and_34_out,
       and_35_out, and_36_out, Cont;

  and and_1 (and_1_out, Entry, 1'b1);
  and and_2 (and_2_out, Cont, 1'b1);
  and and_3 (and_3_out, 1'b1, and_4_out);
  and and_4 (and_4_out, and_1_out, 1'b1);
  and and_5 (and_5_out, 1'b1, and_6_out);
  and and_6 (and_6_out, and_2_out, 1'b1);
  and and_7 (and_7_out, and_3_out, 1'b1);
  and and_8 (and_8_out, and_5_out, 1'b1);
  and and_9 (and_9_out, 1'b1, and_7_out);
  and and_10 (and_10_out, 1'b1, and_8_out);
  and and_11 (and_11_out, 1'b1, and_12_out);
  and and_12 (and_12_out, and_9_out, 1'b1);
  and and_13 (and_13_out, 1'b1, and_14_out);
  and and_14 (and_14_out, and_10_out, 1'b1);
  and and_15 (and_15_out, and_11_out, 1'b1);
  and and_16 (and_16_out, and_13_out, 1'b1);
  and and_17 (and_17_out, 1'b1, and_15_out);
  and and_18 (and_18_out, 1'b1, and_16_out);
  and and_19 (and_19_out, 1'b1, and_20_out);
  and and_20 (and_20_out, and_17_out, 1'b1);
  and and_21 (Delayed_Entry, 1'b1, and_22_out);
  and and_22 (and_22_out, and_18_out, 1'b1);
  and and_23 (and_23_out, and_19_out, 1'b1);
  and and_24 (and_24_out, 1'b1, and_23_out);
  and and_25 (and_25_out, 1'b1, and_26_out);
  and and_26 (and_26_out, and_24_out, 1'b1);
  and and_27 (and_27_out, and_25_out, 1'b1);
  and and_28 (and_28_out, 1'b1, and_27_out);
  and and_29 (and_29_out, 1'b1, and_30_out);
  and and_30 (and_30_out, and_28_out, 1'b1);
  and and_31 (and_31_out, and_29_out, 1'b1);
  and and_32 (and_32_out, 1'b1, and_31_out);
  and and_33 (and_33_out, 1'b1, and_34_out);
  and and_34 (and_34_out, and_32_out, 1'b1);
  and and_35 (and_35_out, and_33_out, 1'b1);
  and and_36 (and_36_out, 1'b1, and_35_out);
  and and_37 (Cont, and_36_out, 1'b1);

  // Notes on the sheet:
  //   Retarda la entrada 37 niveles de compuertas
  //   El sumadorGrupo19 posee 36 niveles
endmodule
