// Logisim project adders.circ as structural Verilog: 3 circuits, main circuit CarrySkipAdder
module CarrySkipAdder (
  input  [15:0] A,
  input  C_in,
  input  [15:0] B,
  output C_out,
  output [15:0] S
);

  wire and_1_out, and_2_out, and_3_out, or_1_out, or_2_out, or_3_out, rippleadder_1_c_out, rippleadder_1_p,
       rippleadder_2_c_out, rippleadder_2_p, rippleadder_3_c_out, rippleadder_3_p, rippleadder_4_p;

  and and_1 (and_1_out, rippleadder_1_p, C_in);
  RippleAdder rippleadder_1 (
    .A(A[3:0]), .B(B[3:0]), .C_in(C_in), .S(S[3:0]), .P(rippleadder_1_p), .C_out(rippleadder_1_c_out));
  or or_1 (or_1_out, rippleadder_1_c_out, and_1_out);
  RippleAdder rippleadder_2 (
    .A(A[7:4]), .B(B[7:4]), .C_in(or_1_out), .S(S[7:4]), .P(rippleadder_2_p), .C_out(rippleadder_2_c_out));
  and and_2 (and_2_out, rippleadder_2_p, or_1_out);
  or or_2 (or_2_out, rippleadder_2_c_out, and_2_out);
  and and_3 (and_3_out, rippleadder_3_p, or_2_out);
  RippleAdder rippleadder_3 (
    .A(A[11:8]), .B(B[11:8]), .C_in(or_2_out), .S(S[11:8]), .P(rippleadder_3_p), .C_out(rippleadder_3_c_out));
  or or_3 (or_3_out, rippleadder_3_c_out, and_3_out);
  // NoConnect on rippleadder_4_p
  RippleAdder rippleadder_4 (
    .A(A[15:12]), .B(B[15:12]), .C_in(or_3_out), .S(S[15:12]), .P(rippleadder_4_p), .C_out(C_out));

  // Other names for the same wires on the sheet: A_0[3:0] = A[3:0]; A_1[3:0] = A[7:4]; A_2[3:0] = A[11:8];
  //   A_3[3:0] = A[15:12]; B_0[3:0] = B[3:0]; B_1[3:0] = B[7:4]; B_2[3:0] = B[11:8]; B_3[3:0] = B[15:12];
  //   S_0[3:0] = S[3:0]; S_1[3:0] = S[7:4]; S_2[3:0] = S[11:8]; S_3[3:0] = S[15:12]
endmodule

module RippleAdder (
  input  [3:0] A,
  input  C_in,
  input  [3:0] B,
  output C_out,
  output [3:0] S,
  output P
);

  wire fulladder_1_c_out, fulladder_1_p, fulladder_2_c_out, fulladder_2_p, fulladder_3_c_out, fulladder_3_p,
       fulladder_4_p;

  FullAdder fulladder_1 (.A(A[0]), .B(B[0]), .C_in(C_in), .C_out(fulladder_1_c_out), .P(fulladder_1_p), .S(S[0]));
  FullAdder fulladder_2 (
    .A(A[1]), .B(B[1]), .C_in(fulladder_1_c_out), .C_out(fulladder_2_c_out), .P(fulladder_2_p), .S(S[1]));
  and and_1 (P, fulladder_1_p, fulladder_2_p, fulladder_3_p, fulladder_4_p);
  FullAdder fulladder_3 (
    .A(A[2]), .B(B[2]), .C_in(fulladder_2_c_out), .C_out(fulladder_3_c_out), .P(fulladder_3_p), .S(S[2]));
  FullAdder fulladder_4 (.A(A[3]), .B(B[3]), .C_in(fulladder_3_c_out), .C_out(C_out), .P(fulladder_4_p), .S(S[3]));
endmodule

module FullAdder (
  input  A,
  input  B,
  input  C_in,
  output S,
  output C_out,
  output P
);

  wire and_1_out, and_2_out, and_3_out;

  xor xor_1 (S, A, B, C_in);
  and and_1 (and_1_out, A, B);
  and and_2 (and_2_out, A, C_in);
  and and_3 (and_3_out, B, C_in);
  or or_1 (P, B, A);
  or or_2 (C_out, and_1_out, and_2_out, and_3_out);
endmodule
