// Logisim project contadorY.circ as structural Verilog: 1 circuit, main circuit contadorY
module contadorY (
  input  Reset,
  input  in_2,
  input  in_3,
  input  Start,
  input  Clock,
  output Carry,
  output [3:0] Y
);

  Counter #(.max('hf), .trigger("falling"), .width(4)) counter_1 (
    .clr(Reset), .load(in_2), .up(in_3), .count(Start), .clk(Clock), .carry(Carry), .Q(Y));  // open: D

  // Notes on the sheet:
  //   in_3: initial=0x1
endmodule
