// Logisim project intentodeCalculoF.circ as structural Verilog: 2 circuits, main circuit main
module main (
  input  [3:0] A,
  input  [3:0] B,
  input  [3:0] C,
  input  [3:0] Y,
  input  [3:0] X,
  input  Clock,
  input  Reset,
  input  Start,
  output [15:0] ValorF
);

  wire and_1_out, CambiarFila, comparator_2_eq, comparator_3_eq, comparator_4_eq, d_ff_1_qn;
  wire [15:0] demultiplexer_1_out1, F_in_R, F_in_T, F_row_in_R, F_row_in_T, F_row_out, multiplexer_4_out,
       PrimerOperando, Salida, SegundoOperando;

  Multiplexer #(.width(16)) multiplexer_1 (.in0(ValorF), .in1(F_row_out), .out(PrimerOperando), .sel(CambiarFila));
  Multiplexer #(.width(16)) multiplexer_2 (
    .in0({{13{A[3]}}, A[2:0]}), .in1({{13{B[3]}}, B[2:0]}), .out(SegundoOperando), .sel(CambiarFila));
  Comparator #(.mode("unsigned"), .width(4)) comparator_1 (.a(X), .b(4'b0000), .eq(CambiarFila));  // open: gt, lt
  Multiplexer #(.width(16)) multiplexer_3 (.in0(F_in_T), .in1(F_row_out), .out(F_in_R), .sel(CambiarFila));
  D_Flip_Flop d_ff_1 (.D(1'b1), .clk(Clock), .Qn(d_ff_1_qn), .reset(Reset));  // open: Q, preset
  Multiplexer #(.width(16)) multiplexer_4 (
    .in0(F_row_in_T), .in1({{13{C[3]}}, C[2:0]}), .out(multiplexer_4_out), .sel(d_ff_1_qn));
  Comparator #(.mode("unsigned"), .width(16)) comparator_2 (
    .a(multiplexer_4_out), .b({16{1'b0}}), .eq(comparator_2_eq));  // open: gt, lt
  CarrySkipAdder carryskipadder_1 (.A(PrimerOperando), .B(SegundoOperando), .S(Salida));  // open: C_in, C_out
  Multiplexer #(.width(16)) multiplexer_5 (
    .in0(multiplexer_4_out), .in1(F_row_out), .out(F_row_in_R), .sel(comparator_2_eq));
  Comparator #(.mode("unsigned"), .width(4)) comparator_3 (.a(X), .b(Y), .eq(comparator_3_eq));  // open: gt, lt
  Comparator #(.mode("unsigned"), .width(4)) comparator_4 (.a(X), .b(4'b0000), .eq(comparator_4_eq));  // open: gt, lt
  Register #(.trigger("falling"), .width(16)) F (.D(F_in_R), .en(Start), .clk(Clock), .Q(ValorF), .clr(Reset));
  Register #(.width(16)) F_row (.D(F_row_in_R), .en(Start), .clk(Clock), .Q(F_row_out), .clr(Reset));
  Demultiplexer #(.width(16)) demultiplexer_1 (
    .out0(F_in_T), .out1(demultiplexer_1_out1), .in(Salida), .sel(CambiarFila));
  Demultiplexer #(.width(16)) demultiplexer_2 (
    .out0(F_row_in_T), .in(demultiplexer_1_out1), .sel(and_1_out));  // open: out1
  and and_1 (and_1_out, comparator_3_eq, comparator_4_eq);

  // Other names for the same wires on the sheet: A_16b[15:0] = {{13{A[3]}}, A[2:0]};
  //   B_16b[15:0] = {{13{B[3]}}, B[2:0]}; C_16b[15:0] = {{13{C[3]}}, C[2:0]}; F_out[15:0] = ValorF
endmodule

module aa (
  input  [3:0] in_1,
  input  [3:0] in_2,
  input  [3:0] in_3,
  input  in_4,
  input  in_5
);

  wire and_1_out, and_2_out, C, d_ff_1_q, d_ff_2_q, not_1_out, not_2_out;
  wire [3:0] X, Y;
  wire [15:0] main_1_valorf;

  Clock clock_1 (.out(C));
  not not_1 (not_1_out, C);
  D_Flip_Flop d_ff_1 (.D(1'b1), .clk(C), .Q(d_ff_1_q), .reset(in_5));  // open: Qn, preset
  and and_1 (and_1_out, not_1_out, d_ff_1_q);
  not not_2 (not_2_out, and_1_out);
  D_Flip_Flop d_ff_2 (.D(1'b1), .clk(and_1_out), .Q(d_ff_2_q), .reset(in_5));  // open: Qn, preset
  and and_2 (and_2_out, not_2_out, d_ff_2_q);
  // Probe on X
  GeneradorPixeles generadorpixeles_1 (.Reset(in_5), .Start(in_4), .Clock(and_2_out), .X(X), .Y(Y));
  // Probe on Y
  // Probe on main_1_valorf
  main main_1 (
    .A(in_1), .B(in_2), .C(in_3), .Y(Y), .X(X), .Clock(C), .Reset(in_5), .Start(in_4), .ValorF(main_1_valorf));

  // Other names for the same wires on the sheet: Reset = in_5; Start = in_4
endmodule
