// Logisim project utilities.circ as structural Verilog: 2 circuits, main circuit FullAdder
module RippleAdder (
  input  [3:0] A,
  input  C_in,
  input  [3:0] B,
  output C_out,
  output [3:0] S,
  output P
);

  wire fulladder_1_c_out, fulladder_1_p, fulladder_2_c_out, fulladder_2_p, fulladder_3_c_out, fulladder_3_p,
       fulladder_4_p;

  FullAdder fulladder_1 (.A(A[0]), .B(B[0]), .C_in(C_in), .C_out(fulladder_1_c_out), .P(fulladder_1_p), .S(S[0]));
  FullAdder fulladder_2 (
    .A(A[1]), .B(B[1]), .C_in(fulladder_1_c_out), .C_out(fulladder_2_c_out), .P(fulladder_2_p), .S(S[1]));
  and and_1 (P, fulladder_1_p, fulladder_2_p, fulladder_3_p, fulladder_4_p);
  FullAdder fulladder_3 (
    .A(A[2]), .B(B[2]), .C_in(fulladder_2_c_out), .C_out(fulladder_3_c_out), .P(fulladder_3_p), .S(S[2]));
  FullAdder fulladder_4 (.A(A[3]), .B(B[3]), .C_in(fulladder_3_c_out), .C_out(C_out), .P(fulladder_4_p), .S(S[3]));
endmodule

module FullAdder (
  input  A,
  input  B,
  input  C_in,
  output S,
  output C_out,
  output P
);

  wire and_1_out, and_2_out, and_3_out;

  xor xor_1 (S, A, B, C_in);
  and and_1 (and_1_out, A, B);
  and and_2 (and_2_out, A, C_in);
  and and_3 (and_3_out, B, C_in);
  or or_1 (P, B, A);
  or or_2 (C_out, and_1_out, and_2_out, and_3_out);
endmodule
